# Fritzing sketch esquema_invernadero (saved by Fritzing 0.9.3b)

parts:
  MH-ET_LIVE_ESP32_DEVKIT1 = MH-ET LIVE ESP32 DEVKIT 38 pins
  DHT1 = DHT11 Humitidy and Temperature Sensor
  R1 = Photocell (LDR) [package=THT]
  Componente1 = FC-28 Soil Hygrometer Module - Probe
  Componente2 = FC-28 Soil Hygrometer Module
  F1 = Fan - Ventilador [package=THT]
  F2 = Fan - Ventilador [package=THT]
  M1 = DC Motor
  J1 = Basic Servo
  LED1 = LED - 5mm [color="Red (633nm)" package="5 mm [THT]"]
  LED2 = RGB LED (com. cathode, rgb) [package="5 mm [THT]"]
  VCC1 = Battery block 9V
  VCC2 = Battery block 9V
  KY-1 = Keyes Relay [package=THT]
  KY-2 = Keyes Relay [package=THT]
  KY-3 = Keyes Relay [package=THT]
  R2 = Resistor [tolerance=±5% resistance=220 package=THT]

nets:
  N1: MH-ET_LIVE_ESP32_DEVKIT1.IO34, Componente2.AO
  N2: MH-ET_LIVE_ESP32_DEVKIT1.IO35, R1.pin_0, R2.Pin_1
  GND: MH-ET_LIVE_ESP32_DEVKIT1.GND#58, DHT1.GND, Componente2.GND, J1.gnd, R2.Pin_0
  N3: MH-ET_LIVE_ESP32_DEVKIT1.IO13, J1.pulse
  VCC: MH-ET_LIVE_ESP32_DEVKIT1.5V, DHT1.VDD, Componente2.VCC, J1.vcc
  N4: MH-ET_LIVE_ESP32_DEVKIT1.IO22, KY-3.signal
  N5: MH-ET_LIVE_ESP32_DEVKIT1.IO21, LED2.red_anode
  N6: MH-ET_LIVE_ESP32_DEVKIT1.GND#70, LED2.common_cathode
  N7: MH-ET_LIVE_ESP32_DEVKIT1.IO19, LED2.green_anode
  N8: MH-ET_LIVE_ESP32_DEVKIT1.IO18, LED2.blue_anode
  N9: MH-ET_LIVE_ESP32_DEVKIT1.IO4, DHT1.DATA
  N10: MH-ET_LIVE_ESP32_DEVKIT1.IO2, KY-2.signal
  N11: MH-ET_LIVE_ESP32_DEVKIT1.IO15, KY-1.signal
  N12: Componente1.POS, Componente2.POS
  N13: Componente1.NEG, Componente2.NEG
  5V: F1.5V, F2.5V
  GND_2: F1.GND, F2.GND
  N14: M1.pin_1, KY-3.NO
  N15: LED1.cathode, KY-2.NO
  N16: VCC1.-, VCC2.-, KY-1.NC, KY-1.C, KY-1.NO, KY-2.C, KY-3.C
  N17: KY-1.power, KY-2.power, KY-3.power

custom parts:
  MH-ET LIVE ESP32 DEVKIT 38 pins: http://mh.nodebb.com/topic/2/mh-et-live-esp32-devkit
  DHT11 Humitidy and Temperature Sensor: DHT11 Humidity and Temperature Sensor
  FC-28 Soil Hygrometer Module - Probe: The FC-28 is a soil hygrometer module that uses the Texas Instruments LM393 comparator chip to provide an analog measurement of soil humidity.
  FC-28 Soil Hygrometer Module: The FC-28 is a soil hygrometer module that uses the Texas Instruments LM393 comparator chip to provide an analog measurement of soil humidity. The digital output is high when soil moisture is over a certain threshold, as determined by adjusting the potentiometer.
  Fan - Ventilador: Ventilador de 2 pines, se encuentra comunmente en computadoras de escritorio
  Battery block 9V: 9 Volt battery block with 200mil pcb footprint spacing and large connection pads
  Keyes Relay: The Keyes 5V relay module is suitable for SCM development, home appliance control. It uses a 5V~12V TIL control signal which can control DC / AC signal.
